# Fritzing sketch Power Switch (saved by Fritzing 0.9.3b)
breadboards: 1

parts:
  Raspberry_Pi = Raspberry Pi 3 [part_number=RPI-3-V1.2]
  S1 = Pushbutton [package="[THT]"]

nets (from the schematic view):
  N1: Raspberry_Pi.GND, S1.Pin_3, S1.Pin_4
  N2: Raspberry_Pi.GPIO18, S1.Pin_1, S1.Pin_2
